// Logisim project D Flip-Flop.circ as structural Verilog: 1 circuit, main circuit main
module main (
  input  in_1,
  output out_2
);

  wire not_1_out, not_3_out, or_1_out, or_2_out;

  not not_1 (not_1_out, in_1);
  not not_2 (out_2, or_1_out);
  or or_1 (or_1_out, not_1_out, not_3_out);
  not not_3 (not_3_out, or_2_out);
  or or_2 (or_2_out, out_2, in_1);
endmodule
