// Logisim project MINIRAM.circ as structural Verilog: 1 circuit, main circuit main
module main (
  input  in_1,
  input  in_2,
  input  in_3,
  input  in_4,
  input  in_5
);

  D_Flip_Flop_main main_1 (.in_1(in_1));  // open: out_2
  D_Flip_Flop_main main_2 (.in_1(in_2));  // open: out_2
  D_Flip_Flop_main main_3 (.in_1(in_3));  // open: out_2
  D_Flip_Flop_main main_4 (.in_1(in_4));  // open: out_2
  // NIBBLE_main main_5: pin names not known
  // NIBBLE_main main_6: pin names not known; wires that end beside it: in_5
  // NIBBLE_main main_7: pin names not known; wires that end beside it: in_5
  // NIBBLE_main main_8: pin names not known; wires that end beside it: in_5
  // NIBBLE_main main_9: pin names not known; wires that end beside it: in_5
  // NIBBLE_main main_10: pin names not known; wires that end beside it: in_5
  // NIBBLE_main main_11: pin names not known; wires that end beside it: in_5
  // NIBBLE_main main_12: pin names not known; wires that end beside it: in_5, in_5
  // NIBBLE_main main_13: pin names not known
  // NIBBLE_main main_14: pin names not known; wires that end beside it: in_5
  // NIBBLE_main main_15: pin names not known; wires that end beside it: in_5
  // NIBBLE_main main_16: pin names not known; wires that end beside it: in_5
  // NIBBLE_main main_17: pin names not known; wires that end beside it: in_5
  // NIBBLE_main main_18: pin names not known; wires that end beside it: in_5
  // NIBBLE_main main_19: pin names not known; wires that end beside it: in_5
  // NIBBLE_main main_20: pin names not known; wires that end beside it: in_5, in_5
endmodule
