// Logisim project S-R Flip FLop.circ as structural Verilog: 1 circuit, main circuit main
module main (
  input  Set,
  input  Reset,
  output Q,
  output Q_prime
);

  wire or_1_out, or_2_out;

  or or_1 (or_1_out, Set, Q_prime);
  or or_2 (or_2_out, Q, Reset);
  not not_1 (Q, or_1_out);
  not not_2 (Q_prime, or_2_out);
endmodule
